# Fritzing sketch design (saved by Fritzing 0.9.3b)
breadboards: 1

parts:
  Part1 = Arduino Uno (Rev3)
  LCD1 = LCD screen
  R1 = Resistor [tolerance=±5% resistance=220 package=THT]
  R2 = Resistor [tolerance=±5% resistance=220 package=THT]
  R3 = Resistor [tolerance=±5% resistance=220 package=THT]
  LED1 = LED - 5mm [color="Red (633nm)" package="5 mm [THT]"]
  LED2 = LED - 5mm [color="Yellow (595nm)" package="5 mm [THT]"]
  LED3 = LED - 5mm [color="Green (570nm)" package="5 mm [THT]"]
  J1 = Piezo Speaker
  U1 = GAS_SENSOR [package=mq-3]
  Part2 = Thumb Joystick
  R4 = Resistor [tolerance=±5% resistance=330 package=THT]

nets:
  N1: Part1.A0, Part2.VERT
  N2: Part1.A1, Part2.HORZ
  N3: Part1.A2, U1.B1
  N4: Part1.D8, LCD1.E
  N5: Part1.D9_PWM, LCD1.DB4
  N6: Part1.D10_PWM/SS, LCD1.DB5
  N7: Part1.D11_PWM/MOSI, LCD1.DB6
  N8: Part1.D12/MISO, LCD1.DB7
  GND: Part1.GND, LCD1.VSS, LCD1.LED-, U1.H1, Part2.GND, R4.Pin_0
  N9: Part1.D2, LED1.cathode
  N10: Part1.D3_PWM, LED2.cathode
  N11: Part1.D4, LED3.cathode
  N12: Part1.D5_PWM, Part2.SEL
  N13: Part1.D6_PWM, J1.pin1
  N14: Part1.D7, LCD1.RS
  5V: Part1.5V, LCD1.VDD, LCD1.R/W, LCD1.LED+, R1.Pin_0, R2.Pin_0, R3.Pin_0, J1.pin2, U1.H2, Part2.VCC
  N15: LCD1.V0, R4.Pin_1
  N16: R1.Pin_1, LED1.anode
  N17: R2.Pin_1, LED2.anode
  N18: R3.Pin_1, LED3.anode

notes:
  De pet al cache
  MQ-7
